// Logisim project branch-comp.circ as structural Verilog: 1 circuit, main circuit branch_comp
module branch_comp (
  input  [31:0] BrData1,
  input  [31:0] BrData2,
  input  BrUn,
  output BrEq,
  output BrLt
);

  wire LT_signed, LT_unsigned;

  Comparator #(.width(32)) comparator_1 (.a(BrData1), .b(BrData2), .eq(BrEq), .lt(LT_signed));  // open: gt
  Comparator #(.mode("unsigned"), .width(32)) comparator_2 (
    .a(BrData1), .b(BrData2), .lt(LT_unsigned));  // open: gt, eq
  Multiplexer multiplexer_1 (.in0(LT_signed), .in1(LT_unsigned), .out(BrLt), .sel(BrUn));

  // Notes on the sheet:
  //   INPUTS to your circuit
  //   DON'T CHANGE THE LOCATIONS OF THE INPUTS AND OUTPUTS!
  //   OUTPUT from your circuit
endmodule
