// Logisim project control-logic.circ as structural Verilog: 1 circuit, main circuit control_logic
module control_logic (
  input  [31:0] Instruction,
  input  BrEq,
  input  BrLt,
  output PCSel,
  output RegWEn,
  output [2:0] ImmSel,
  output BrUn,
  output ASel,
  output BSel,
  output [3:0] ALUSel,
  output MemRW,
  output [1:0] WBSel,
  output is_auipc,
  output is_jalr
);

  wire addr_bit0, addr_bit0_pre, addr_bit0_pre_ls, addr_bit0_pre_uj, addr_bit1, addr_bit1_pre_ls,
       addr_bit1_pre_uj, addr_bit2, addr_bit2_pre, addr_bit2_pre_ls, addr_bit3, addr_bit3_pre,
       addr_bit3_pre_ls, addr_bit3_pre_uj, addr_bit4, addr_bit4_pre, addr_bit4_pre_ls, b_beq, b_bge, b_bgeu,
       b_blt, b_bltu, b_bne, br_bit0, comparator_1_eq, is_branch, is_jal, is_jal_or_jalr, is_load,
       is_load_or_store, is_lui, is_lui_or_auipc_a, is_store, is_uj_type, m_add, m_and, m_andi, m_mul,
       m_mulh, m_mulhu, m_or, m_ori, m_sll, m_slli, m_slt, m_slti, m_sra, m_srai, m_srl, m_srli, m_sub,
       m_xor, m_xori, not_BrEq, not_BrLt, or_3_out, or_4_out, or_5_out, or_6_out, or_9_out, or_10_out,
       pcsel_beq, pcsel_bge, pcsel_bgeu, pcsel_blt, pcsel_bltu, pcsel_bne, PCSel_branch_pre, uj_bit0;
  wire [5:0] rom_addr;
  wire [15:14] rom_1_data;

  Comparator #(.width(11)) comparator_1 (
    .a({Instruction[30], Instruction[14:12], Instruction[6:0]}), .b(11'h13), .eq(comparator_1_eq));  // open: gt, lt
  Comparator #(.width(11)) comparator_2 (
    .a({Instruction[30], Instruction[14:12], Instruction[6:0]}), .b(11'h93), .eq(m_slli));  // open: gt, lt
  Comparator #(.width(11)) comparator_3 (
    .a({Instruction[30], Instruction[14:12], Instruction[6:0]}), .b(11'h113), .eq(m_slti));  // open: gt, lt
  Comparator #(.width(11)) comparator_4 (
    .a({Instruction[30], Instruction[14:12], Instruction[6:0]}), .b(11'h213), .eq(m_xori));  // open: gt, lt
  Comparator #(.width(12)) comparator_5 (
    .a({Instruction[25], Instruction[30], Instruction[14:12], Instruction[6:0]}), .b(12'h33), .eq(m_add));  // open: gt, lt
  Comparator #(.width(12)) comparator_6 (
    .a({Instruction[25], Instruction[30], Instruction[14:12], Instruction[6:0]}), .b(12'h433), .eq(m_sub));  // open: gt, lt
  Comparator #(.width(12)) comparator_7 (
    .a({Instruction[25], Instruction[30], Instruction[14:12], Instruction[6:0]}), .b(12'hb3), .eq(m_sll));  // open: gt, lt
  Comparator #(.width(12)) comparator_8 (
    .a({Instruction[25], Instruction[30], Instruction[14:12], Instruction[6:0]}), .b(12'h133), .eq(m_slt));  // open: gt, lt
  or or_1 (addr_bit3_pre, m_slt, m_mul, m_mulh, m_mulhu);
  assign rom_addr = {{1{1'b0}}, {addr_bit4, addr_bit3, addr_bit2, addr_bit1, addr_bit0}};  // Bit_Extender bit_extender_1
  ROM #(.addrWidth(6), .dataWidth(16)) rom_1 (
    .addr(rom_addr), .data({rom_1_data, WBSel, MemRW, ALUSel, BSel, ASel, BrUn, ImmSel, RegWEn}));
  Comparator #(.width(11)) comparator_9 (
    .a({Instruction[30], Instruction[14:12], Instruction[6:0]}), .b(11'h393), .eq(m_andi));  // open: gt, lt
  Comparator #(.width(11)) comparator_10 (
    .a({Instruction[30], Instruction[14:12], Instruction[6:0]}), .b(11'h293), .eq(m_srli));  // open: gt, lt
  Comparator #(.width(11)) comparator_11 (
    .a({Instruction[30], Instruction[14:12], Instruction[6:0]}), .b(11'h693), .eq(m_srai));  // open: gt, lt
  Comparator #(.width(11)) comparator_12 (
    .a({Instruction[30], Instruction[14:12], Instruction[6:0]}), .b(11'h313), .eq(m_ori));  // open: gt, lt
  Comparator #(.width(12)) comparator_13 (
    .a({Instruction[25], Instruction[30], Instruction[14:12], Instruction[6:0]}), .b(12'h333), .eq(m_or));  // open: gt, lt
  or or_2 (addr_bit4_pre, m_add, m_sub, m_and, m_or, m_xor, m_sll, m_srl, m_sra, m_slt, m_mul, m_mulh, m_mulhu);
  Comparator #(.width(12)) comparator_14 (
    .a({Instruction[25], Instruction[30], Instruction[14:12], Instruction[6:0]}), .b(12'h233), .eq(m_xor));  // open: gt, lt
  Comparator #(.width(12)) comparator_15 (
    .a({Instruction[25], Instruction[30], Instruction[14:12], Instruction[6:0]}), .b(12'h2b3), .eq(m_srl));  // open: gt, lt
  Comparator #(.width(12)) comparator_16 (
    .a({Instruction[25], Instruction[30], Instruction[14:12], Instruction[6:0]}), .b(12'h6b3), .eq(m_sra));  // open: gt, lt
  or or_3 (or_3_out, m_srli, m_ori, m_andi, m_srai);
  or or_4 (or_4_out, m_xor, m_sll, m_srl, m_sra);
  or or_5 (or_5_out, m_mul, m_sra, m_sll, m_or, m_sub, m_mulhu);
  or or_6 (or_6_out, m_srai, m_xori, m_slli, m_andi);
  Comparator #(.width(12)) comparator_17 (
    .a({Instruction[25], Instruction[30], Instruction[14:12], Instruction[6:0]}), .b(12'h3b3), .eq(m_and));  // open: gt, lt
  Comparator #(.width(12)) comparator_18 (
    .a({Instruction[25], Instruction[30], Instruction[14:12], Instruction[6:0]}), .b(12'h833), .eq(m_mul));  // open: gt, lt
  Comparator #(.width(12)) comparator_19 (
    .a({Instruction[25], Instruction[30], Instruction[14:12], Instruction[6:0]}), .b(12'h8b3), .eq(m_mulh));  // open: gt, lt
  Comparator #(.width(12)) comparator_20 (
    .a({Instruction[25], Instruction[30], Instruction[14:12], Instruction[6:0]}), .b(12'h9b3), .eq(m_mulhu));  // open: gt, lt
  or or_7 (addr_bit2_pre, or_3_out, or_4_out);
  or or_8 (addr_bit0_pre, or_5_out, or_6_out);
  or or_9 (or_9_out, m_xori, m_slti, m_ori, m_andi);
  or or_10 (or_10_out, m_mulh, m_sra, m_srl, m_or, m_and, m_mulhu);
  or or_11 (addr_bit1_pre_ls, or_9_out, or_10_out);
  Comparator #(.width(10)) comparator_21 (
    .a({Instruction[14:12], Instruction[6:0]}), .b(10'h63), .eq(b_beq));  // open: gt, lt
  Comparator #(.width(10)) comparator_22 (
    .a({Instruction[14:12], Instruction[6:0]}), .b(10'he3), .eq(b_bne));  // open: gt, lt
  Comparator #(.width(10)) comparator_23 (
    .a({Instruction[14:12], Instruction[6:0]}), .b(10'h263), .eq(b_blt));  // open: gt, lt
  Comparator #(.width(10)) comparator_24 (
    .a({Instruction[14:12], Instruction[6:0]}), .b(10'h2e3), .eq(b_bge));  // open: gt, lt
  Comparator #(.width(10)) comparator_25 (
    .a({Instruction[14:12], Instruction[6:0]}), .b(10'h363), .eq(b_bltu));  // open: gt, lt
  Comparator #(.width(10)) comparator_26 (
    .a({Instruction[14:12], Instruction[6:0]}), .b(10'h3e3), .eq(b_bgeu));  // open: gt, lt
  or or_12 (br_bit0, b_bltu, b_bgeu);
  or or_13 (is_branch, b_beq, b_bne, b_blt, b_bge, b_bltu, b_bgeu);
  or or_14 (addr_bit4_pre_ls, addr_bit4_pre, is_branch);
  or or_15 (addr_bit2_pre_ls, addr_bit2_pre, is_branch);
  xor xor_1 (not_BrEq, BrEq, 1'b1);
  or or_16 (addr_bit3_pre_ls, addr_bit3_pre, is_branch);
  or or_17 (addr_bit0_pre_ls, addr_bit0_pre, br_bit0);
  xor xor_2 (not_BrLt, BrLt, 1'b1);
  and and_1 (pcsel_beq, b_beq, BrEq);
  and and_2 (pcsel_bltu, b_bltu, BrLt);
  and and_3 (pcsel_bne, b_bne, not_BrEq);
  and and_4 (pcsel_blt, b_blt, BrLt);
  and and_5 (pcsel_bge, b_bge, not_BrLt);
  and and_6 (pcsel_bgeu, b_bgeu, not_BrLt);
  or or_18 (PCSel_branch_pre, pcsel_beq, pcsel_bne, pcsel_blt, pcsel_bge, pcsel_bltu, pcsel_bgeu);
  Comparator #(.width(7)) comparator_27 (.a(Instruction[6:0]), .b(7'b0000011), .eq(is_load));  // open: gt, lt
  Comparator #(.width(7)) comparator_28 (.a(Instruction[6:0]), .b(7'b0100011), .eq(is_store));  // open: gt, lt
  or or_19 (is_load_or_store, is_load, is_store);
  or or_20 (addr_bit3_pre_uj, addr_bit3_pre_ls, is_load_or_store);
  or or_21 (addr_bit1_pre_uj, addr_bit1_pre_ls, is_load_or_store);
  or or_22 (addr_bit0_pre_uj, addr_bit0_pre_ls, is_store);
  or or_23 (addr_bit4, addr_bit4_pre_ls, is_load_or_store);
  or or_24 (addr_bit2, addr_bit2_pre_ls, is_load_or_store);
  Comparator #(.width(7)) comparator_29 (.a(Instruction[6:0]), .b(7'b1101111), .eq(is_jal));  // open: gt, lt
  Comparator #(.width(7)) comparator_30 (.a(Instruction[6:0]), .b(7'b0110111), .eq(is_lui));  // open: gt, lt
  Comparator #(.width(7)) comparator_31 (.a(Instruction[6:0]), .b(7'b0010111), .eq(is_auipc));  // open: gt, lt
  Comparator #(.width(7)) comparator_32 (.a(Instruction[6:0]), .b(7'b1100111), .eq(is_jalr));  // open: gt, lt
  or or_25 (is_lui_or_auipc_a, is_lui, is_auipc);
  or or_26 (is_jal_or_jalr, is_jal, is_jalr);
  or or_27 (uj_bit0, is_auipc, is_jalr);
  or or_28 (is_uj_type, is_lui_or_auipc_a, is_jal_or_jalr);
  or or_29 (addr_bit0, addr_bit0_pre_uj, uj_bit0);
  or or_30 (PCSel, PCSel_branch_pre, is_jal_or_jalr);
  or or_31 (addr_bit1, addr_bit1_pre_uj, is_jal_or_jalr);
  or or_32 (addr_bit3, addr_bit3_pre_uj, is_uj_type);

  // Other names for the same wires on the sheet: opcode7_ls[6:0] = Instruction[6:0];
  //   opcode7_uj[6:0] = Instruction[6:0]

  // Notes on the sheet:
  //   INPUTS to your circuit
  //   Connect ROM Input here ->
  //   contents of rom_1 (hex, n*v repeats v):
  //   1 81 101 201 281 681 301 381 3007 7 2009 2001 4*0 41 641 3c1 341 241 c1 2c1 6c1 141 441 4c1 5c1 4 14
  //   1001 802
  //   ROM FOR CONTROL LOGIC
  //   DON'T CHANGE THE LOCATIONS OF THE INPUTS AND OUTPUTS!
  //   This is only if you choose to do the ROM option
  //   CONNECT
  //   WIRE
  //   TO
  //   USE
  //   ROM
  //   OUTPUT from your circuit
  //   Reminder: If using ROM, use combinational logic for PCSel
endmodule
