// Logisim project cpu.circ as structural Verilog: 1 circuit, main circuit cpu
module cpu (
  input  clk,
  input  [31:0] Instruction,
  input  [31:0] MemReadData,
  output [31:0] MemAddress,
  output [31:0] ProgramCounter,
  output [31:0] ra,
  output [31:0] sp,
  output [31:0] t0,
  output [31:0] t1,
  output [31:0] t2,
  output [31:0] s0,
  output [31:0] s1,
  output [31:0] a0,
  output [3:0] MemWriteMask,
  output [31:0] MemWriteData
);

  wire BrEq, BrLt, BrUn, BSel, is_jalr, MemRW, not_BSel, not_is_jalr, PCSel, RegWEn;
  wire [1:0] WBSel;
  wire [2:0] control_logic_1_immsel;
  wire [3:0] ALUSel;
  wire [31:0] BSel_mask, bsel_result, Immediate, jalr_mask, jump_target, new_pc_imm, nextPc, not_BSel_mask,
       not_jalr_mask, partial_load_1_datatoreg, Pcplus4, ReadData1, ReadData2, term_imm, term_jalr,
       term_pcimm, term_rd2, wbsel_result_g;

  Register #(.width(32)) PC (.D(nextPc), .clk(clk), .Q(ProgramCounter));  // open: en, clr
  Adder #(.width(32)) adder_1 (.a(ProgramCounter), .b(32'h4), .out(Pcplus4));  // open: cin, cout
  Adder #(.width(32)) adder_2 (.a(ProgramCounter), .b(Immediate), .out(new_pc_imm));  // open: cin, cout
  Multiplexer #(.width(32)) multiplexer_1 (.in0(Pcplus4), .in1(jump_target), .out(nextPc), .sel(PCSel));
  control_logic control_logic_1 (
    .Instruction(Instruction), .BrEq(BrEq), .BrLt(BrLt), .PCSel(PCSel), .RegWEn(RegWEn),
    .ImmSel(control_logic_1_immsel), .BrUn(BrUn), .BSel(BSel), .ALUSel(ALUSel), .MemRW(MemRW), .WBSel(WBSel),
    .is_jalr(is_jalr));  // open: ASel, is_auipc
  regfile regfile_1 (
    .ReadIndex1(Instruction[19:15]), .ReadIndex2(Instruction[24:20]), .WriteIndex(Instruction[11:7]),
    .WriteData(wbsel_result_g), .RegWEn(RegWEn), .clk(clk), .ra(ra), .sp(sp), .t0(t0), .t1(t1), .t2(t2),
    .s0(s0), .s1(s1), .a0(a0), .ReadData1(ReadData1), .ReadData2(ReadData2));
  imm_gen imm_gen_1 (.Instruction(Instruction), .ImmSel(control_logic_1_immsel), .Immediate(Immediate));
  // XOR_Gate xor_1 has open pins: out=not_BSel
  assign BSel_mask = {{31{BSel}}, BSel};  // Bit_Extender bit_extender_1
  assign not_BSel_mask = {{31{not_BSel}}, not_BSel};  // Bit_Extender bit_extender_2
  alu alu_1 (.A(ReadData1), .B(bsel_result), .ALUSel(ALUSel), .ALUResult(MemAddress));
  branch_comp branch_comp_1 (.BrData1(ReadData1), .BrData2(ReadData2), .BrUn(BrUn), .BrEq(BrEq), .BrLt(BrLt));
  assign term_rd2 = ReadData2 & BSel_mask;  // AND_Gate and_1, 32 bits wide
  assign term_imm = Immediate & not_BSel_mask;  // AND_Gate and_2, 32 bits wide
  Multiplexer #(.select(2), .width(32)) multiplexer_2 (
    .in0(MemAddress), .in1(partial_load_1_datatoreg), .in2(Pcplus4), .in3(Immediate), .out(wbsel_result_g),
    .sel(WBSel));
  assign bsel_result = term_rd2 | term_imm;  // OR_Gate or_1, 32 bits wide
  // XOR_Gate xor_2 has open pins: out=not_is_jalr
  partial_store partial_store_1 (
    .Instruction(Instruction), .MemAddress(MemAddress), .DataFromReg(ReadData2), .MemRW(MemRW),
    .MemWriteMask(MemWriteMask), .DataToMem(MemWriteData));
  partial_load partial_load_1 (
    .Instruction(Instruction), .MemAddress(MemAddress), .DataFromMem(MemReadData),
    .DataToReg(partial_load_1_datatoreg));
  assign jalr_mask = {{31{is_jalr}}, is_jalr};  // Bit_Extender bit_extender_3
  assign not_jalr_mask = {{31{not_is_jalr}}, not_is_jalr};  // Bit_Extender bit_extender_4
  assign term_jalr = MemAddress & jalr_mask;  // AND_Gate and_3, 32 bits wide
  assign term_pcimm = new_pc_imm & not_jalr_mask;  // AND_Gate and_4, 32 bits wide
  assign jump_target = term_jalr | term_pcimm;  // OR_Gate or_2, 32 bits wide

  // Other names for the same wires on the sheet: alu_result_jalr[31:0] = MemAddress

  // Notes on the sheet:
  //   To IMEM
  //   IMEM (do **NOT** move this)
  //   From IMEM
  //   Inputs/Outputs for testing. Do **NOT** move these.
  //   It is OK to move the PC, RegFile, ALU, MEM, Branch Comp, Imm Gen, Partial Load, Partial Store and Control Logic to wherever is most convenient for you when constructing your CPU, and to delete this text
  //   To DMEM
  //   DMEM (do **NOT** move this)
  //   From DMEM
endmodule
