// Logisim project partial-store.circ as structural Verilog: 1 circuit, main circuit partial_store
module partial_store (
  input  [31:0] Instruction,
  input  [31:0] MemAddress,
  input  [31:0] DataFromReg,
  input  MemRW,
  output [3:0] MemWriteMask,
  output [31:0] DataToMem
);

  wire [3:0] comparator_1_eq, multiplexer_1_out, multiplexer_2_out;

  Comparator #(.width(2)) comparator_1 (.a(MemAddress[1:0]), .b(2'b00), .eq(comparator_1_eq[0]));  // open: gt, lt
  Comparator #(.width(2)) comparator_2 (.a(MemAddress[1:0]), .b(2'b01), .eq(comparator_1_eq[1]));  // open: gt, lt
  Comparator #(.width(2)) comparator_3 (.a(MemAddress[1:0]), .b(2'b10), .eq(comparator_1_eq[2]));  // open: gt, lt
  Comparator #(.width(2)) comparator_4 (.a(MemAddress[1:0]), .b(2'b11), .eq(comparator_1_eq[3]));  // open: gt, lt
  Multiplexer #(.width(4)) multiplexer_1 (.in0(4'b0011), .in1(4'b1100), .out(multiplexer_1_out), .sel(MemAddress[1]));
  Multiplexer #(.select(2), .width(4)) multiplexer_2 (
    .in0(comparator_1_eq), .in1(multiplexer_1_out), .in2(4'b1111), .in3(4'b0000), .out(multiplexer_2_out),
    .sel(Instruction[13:12]));
  Multiplexer #(.width(4)) multiplexer_3 (.in0(4'b0000), .in1(multiplexer_2_out), .out(MemWriteMask), .sel(MemRW));
  Multiplexer #(.select(2), .width(32)) multiplexer_4 (
    .in0({DataFromReg[7:0], DataFromReg[7:0], DataFromReg[7:0], DataFromReg[7:0]}),
    .in1({DataFromReg[15:0], DataFromReg[15:0]}), .in2(DataFromReg), .in3({32{1'b0}}), .out(DataToMem),
    .sel(Instruction[13:12]));

  // Notes on the sheet:
  //   INPUTS to your circuit
  //   DON'T CHANGE THE LOCATIONS OF THE INPUTS AND OUTPUTS!
  //   OUTPUT from your circuit
endmodule
