// Logisim project regfile.circ as structural Verilog: 1 circuit, main circuit regfile
module regfile (
  input  [4:0] ReadIndex1,
  input  [4:0] ReadIndex2,
  input  [4:0] WriteIndex,
  input  [31:0] WriteData,
  input  RegWEn,
  input  clk,
  output [31:0] ra,
  output [31:0] sp,
  output [31:0] t0,
  output [31:0] t1,
  output [31:0] t2,
  output [31:0] s0,
  output [31:0] s1,
  output [31:0] a0,
  output [31:0] ReadData1,
  output [31:0] ReadData2
);

  wire en1, en2, en3, en4, en5, en6, en7, en8, en9, en10, en11, en12, en13, en14, en15, en16, en17, en18,
       en19, en20, en21, en22, en23, en24, en25, en26, en27, en28, en29, en30, en31;
  wire [31:0] reg3, reg4, reg11, reg12, reg13, reg14, reg15, reg16, reg17, reg18, reg19, reg20, reg21, reg22,
       reg23, reg24, reg25, reg26, reg27, reg28, reg29, reg30, reg31;

  Decoder #(.select(5)) decoder_1 (
    .out1(en1), .out2(en2), .out3(en3), .out4(en4), .out5(en5), .out6(en6), .out7(en7), .out8(en8),
    .out9(en9), .out10(en10), .out11(en11), .out12(en12), .out13(en13), .out14(en14), .out15(en15),
    .out16(en16), .out17(en17), .out18(en18), .out19(en19), .out20(en20), .out21(en21), .out22(en22),
    .out23(en23), .out24(en24), .out25(en25), .out26(en26), .out27(en27), .out28(en28), .out29(en29),
    .out30(en30), .out31(en31), .sel(WriteIndex), .en(RegWEn));  // open: out0
  Multiplexer #(.select(5), .width(32)) multiplexer_1 (
    .in0({32{1'b0}}), .in1(ra), .in2(sp), .in3(reg3), .in4(reg4), .in5(t0), .in6(t1), .in7(t2), .in8(s0),
    .in9(s1), .in10(a0), .in11(reg11), .in12(reg12), .in13(reg13), .in14(reg14), .in15(reg15), .in16(reg16),
    .in17(reg17), .in18(reg18), .in19(reg19), .in20(reg20), .in21(reg21), .in22(reg22), .in23(reg23),
    .in24(reg24), .in25(reg25), .in26(reg26), .in27(reg27), .in28(reg28), .in29(reg29), .in30(reg30),
    .in31(reg31), .out(ReadData1), .sel(ReadIndex1));
  Register #(.width(32)) register_1 (.D(WriteData), .en(en24), .clk(clk), .Q(reg24));  // open: clr
  Register #(.width(32)) register_2 (.D(WriteData), .en(en26), .clk(clk), .Q(reg26));  // open: clr
  Register #(.width(32)) register_3 (.D(WriteData), .en(en28), .clk(clk), .Q(reg28));  // open: clr
  Register #(.width(32)) register_4 (.D(WriteData), .en(en30), .clk(clk), .Q(reg30));  // open: clr
  Register #(.width(32)) register_5 (.D(WriteData), .en(en3), .clk(clk), .Q(reg3));  // open: clr
  Register #(.width(32)) register_6 (.D(WriteData), .en(en1), .clk(clk), .Q(ra));  // open: clr
  Multiplexer #(.select(5), .width(32)) multiplexer_2 (
    .in0({32{1'b0}}), .in1(ra), .in2(sp), .in3(reg3), .in4(reg4), .in5(t0), .in6(t1), .in7(t2), .in8(s0),
    .in9(s1), .in10(a0), .in11(reg11), .in12(reg12), .in13(reg13), .in14(reg14), .in15(reg15), .in16(reg16),
    .in17(reg17), .in18(reg18), .in19(reg19), .in20(reg20), .in21(reg21), .in22(reg22), .in23(reg23),
    .in24(reg24), .in25(reg25), .in26(reg26), .in27(reg27), .in28(reg28), .in29(reg29), .in30(reg30),
    .in31(reg31), .out(ReadData2), .sel(ReadIndex2));
  Register #(.width(32)) register_7 (.D(WriteData), .en(en25), .clk(clk), .Q(reg25));  // open: clr
  Register #(.width(32)) register_8 (.D(WriteData), .en(en27), .clk(clk), .Q(reg27));  // open: clr
  Register #(.width(32)) register_9 (.D(WriteData), .en(en29), .clk(clk), .Q(reg29));  // open: clr
  Register #(.width(32)) register_10 (.D(WriteData), .en(en31), .clk(clk), .Q(reg31));  // open: clr
  Register #(.width(32)) register_11 (.D(WriteData), .en(en2), .clk(clk), .Q(sp));  // open: clr
  Register #(.width(32)) register_12 (.D(WriteData), .en(en4), .clk(clk), .Q(reg4));  // open: clr
  Register #(.width(32)) register_13 (.D(WriteData), .en(en6), .clk(clk), .Q(t1));  // open: clr
  Register #(.width(32)) register_14 (.D(WriteData), .en(en8), .clk(clk), .Q(s0));  // open: clr
  Register #(.width(32)) register_15 (.D(WriteData), .en(en10), .clk(clk), .Q(a0));  // open: clr
  Register #(.width(32)) register_16 (.D(WriteData), .en(en12), .clk(clk), .Q(reg12));  // open: clr
  Register #(.width(32)) register_17 (.D(WriteData), .en(en14), .clk(clk), .Q(reg14));  // open: clr
  Register #(.width(32)) register_18 (.D(WriteData), .en(en16), .clk(clk), .Q(reg16));  // open: clr
  Register #(.width(32)) register_19 (.D(WriteData), .en(en18), .clk(clk), .Q(reg18));  // open: clr
  Register #(.width(32)) register_20 (.D(WriteData), .en(en20), .clk(clk), .Q(reg20));  // open: clr
  Register #(.width(32)) register_21 (.D(WriteData), .en(en22), .clk(clk), .Q(reg22));  // open: clr
  Register #(.width(32)) register_22 (.D(WriteData), .en(en5), .clk(clk), .Q(t0));  // open: clr
  Register #(.width(32)) register_23 (.D(WriteData), .en(en7), .clk(clk), .Q(t2));  // open: clr
  Register #(.width(32)) register_24 (.D(WriteData), .en(en9), .clk(clk), .Q(s1));  // open: clr
  Register #(.width(32)) register_25 (.D(WriteData), .en(en11), .clk(clk), .Q(reg11));  // open: clr
  Register #(.width(32)) register_26 (.D(WriteData), .en(en13), .clk(clk), .Q(reg13));  // open: clr
  Register #(.width(32)) register_27 (.D(WriteData), .en(en15), .clk(clk), .Q(reg15));  // open: clr
  Register #(.width(32)) register_28 (.D(WriteData), .en(en17), .clk(clk), .Q(reg17));  // open: clr
  Register #(.width(32)) register_29 (.D(WriteData), .en(en19), .clk(clk), .Q(reg19));  // open: clr
  Register #(.width(32)) register_30 (.D(WriteData), .en(en21), .clk(clk), .Q(reg21));  // open: clr
  Register #(.width(32)) register_31 (.D(WriteData), .en(en23), .clk(clk), .Q(reg23));  // open: clr

  // Other names for the same wires on the sheet: reg1[31:0] = ra; reg2[31:0] = sp; reg5[31:0] = t0; reg6[31:0] = t1;
  //   reg7[31:0] = t2; reg8[31:0] = s0; reg9[31:0] = s1; reg10[31:0] = a0

  // Notes on the sheet:
  //   INPUTS to your circuit
  //   DON'T CHANGE THE LOCATIONS OF THE INPUTS AND OUTPUTS!
  //   These are DEBUG/TEST outputs from your circuit.
  //   OUTPUTS from your circuit
endmodule
